// Logisim project teste1.circ as structural Verilog: 5 circuits, main circuit main
module main (
  input  in_1,
  input  in_2,
  input  in_3,
  input  in_4,
  input  in_5,
  input  in_6,
  input  in_7,
  input  in_8,
  input  in_9,
  input  in_10,
  input  in_11,
  input  in_12
);

  wire and_1_out, and_2_out, and_3_out, button_1_out, or_1_out, s1_1_s1, s1_2_s1, s2_1_s2, s2_2_s2, s3_1_s3,
       s3_2_s3, s4_1_s4, s4_2_s4, xnor_1_out, xnor_2_out, xnor_3_out, xnor_4_out, xnor_5_out, xnor_6_out,
       xnor_7_out, xnor_8_out;

  S1 s1_1 (.A(in_1), .B(in_2), .C(in_3), .D(in_4), .S1(s1_1_s1));
  S2 s2_1 (.a(in_1), .b(in_2), .c(in_3), .d(in_4), .S2(s2_1_s2));
  S3 s3_1 (.a(in_1), .b(in_2), .c(in_3), .d(in_4), .S3(s3_1_s3));
  S4 s4_1 (.a(in_1), .b(in_2), .c(in_3), .d(in_4), .S4(s4_1_s4));
  S1 s1_2 (.A(in_5), .B(in_6), .C(in_7), .D(in_8), .S1(s1_2_s1));
  S2 s2_2 (.a(in_5), .b(in_6), .c(in_7), .d(in_8), .S2(s2_2_s2));
  S3 s3_2 (.a(in_5), .b(in_6), .c(in_7), .d(in_8), .S3(s3_2_s3));
  S4 s4_2 (.a(in_5), .b(in_6), .c(in_7), .d(in_8), .S4(s4_2_s4));
  xnor xnor_1 (xnor_1_out, s4_2_s4, in_12);
  xnor xnor_2 (xnor_2_out, s1_2_s1, in_9);
  xnor xnor_3 (xnor_3_out, s2_2_s2, in_10);
  xnor xnor_4 (xnor_4_out, s3_2_s3, in_11);
  and and_1 (and_1_out, xnor_2_out, xnor_3_out, xnor_4_out, xnor_1_out);
  xnor xnor_5 (xnor_5_out, s1_1_s1, in_9);
  xnor xnor_6 (xnor_6_out, s2_1_s2, in_10);
  xnor xnor_7 (xnor_7_out, s3_1_s3, in_11);
  xnor xnor_8 (xnor_8_out, s4_1_s4, in_12);
  and and_2 (and_2_out, xnor_5_out, xnor_6_out, xnor_7_out, xnor_8_out);
  or or_1 (or_1_out, and_2_out, and_1_out);
  Button button_1 (.out(button_1_out));
  and and_3 (and_3_out, or_1_out, button_1_out);
  LED led_1 (.in(and_3_out));
endmodule

module S1 (
  input  A,
  input  B,
  input  C,
  input  D,
  output S1
);

  wire and_1_out, and_2_out, and_3_out, and_4_out, not_1_out, not_2_out, not_3_out, not_4_out;

  not not_1 (not_1_out, B);
  and and_1 (and_1_out, not_1_out, D);
  and and_2 (and_2_out, B, C, not_2_out);
  not not_2 (not_2_out, D);
  and and_3 (and_3_out, A, not_3_out, not_4_out);
  not not_3 (not_3_out, B);
  not not_4 (not_4_out, C);
  and and_4 (and_4_out, A, B, C);
  or or_1 (S1, and_1_out, and_2_out, and_3_out, and_4_out);
endmodule

module S2 (
  input  a,
  input  b,
  input  c,
  input  d,
  output S2
);

  wire and_1_out, and_2_out, and_3_out, and_4_out, not_1_out, not_2_out, not_3_out, not_4_out, not_5_out;

  not not_1 (not_1_out, b);
  and and_1 (and_1_out, not_1_out, not_2_out);
  not not_2 (not_2_out, c);
  not not_3 (not_3_out, c);
  and and_2 (and_2_out, not_3_out, d);
  and and_3 (and_3_out, a, not_4_out);
  not not_4 (not_4_out, c);
  and and_4 (and_4_out, a, not_5_out, d);
  not not_5 (not_5_out, b);
  or or_1 (S2, and_1_out, and_2_out, and_3_out, and_4_out);
endmodule

module S3 (
  input  a,
  input  b,
  input  c,
  input  d,
  output S3
);

  wire and_1_out, and_2_out, and_3_out, and_4_out, and_5_out, not_1_out, not_2_out, not_3_out, not_4_out,
       not_5_out, not_6_out, not_7_out, not_8_out, not_9_out, not_10_out;

  not not_1 (not_1_out, a);
  not not_2 (not_2_out, b);
  not not_3 (not_3_out, d);
  not not_4 (not_4_out, b);
  not not_5 (not_5_out, c);
  not not_6 (not_6_out, d);
  not not_7 (not_7_out, b);
  not not_8 (not_8_out, a);
  not not_9 (not_9_out, c);
  not not_10 (not_10_out, d);
  and and_1 (and_1_out, not_1_out, not_2_out, not_3_out);
  and and_2 (and_2_out, not_4_out, not_5_out, not_6_out);
  and and_3 (and_3_out, not_7_out, c, d);
  and and_4 (and_4_out, not_8_out, b, not_9_out);
  and and_5 (and_5_out, a, b, c, not_10_out);
  or or_1 (S3, and_1_out, and_2_out, and_3_out, and_4_out, and_5_out);
endmodule

module S4 (
  input  a,
  input  b,
  input  c,
  input  d,
  output S4
);

  wire and_1_out, and_2_out, and_3_out, and_4_out, and_5_out, not_1_out, not_2_out, not_3_out, not_4_out,
       not_5_out, not_6_out, not_7_out, not_8_out, not_9_out;

  not not_1 (not_1_out, a);
  not not_2 (not_2_out, b);
  not not_3 (not_3_out, c);
  not not_4 (not_4_out, a);
  not not_5 (not_5_out, d);
  not not_6 (not_6_out, b);
  not not_7 (not_7_out, d);
  not not_8 (not_8_out, d);
  not not_9 (not_9_out, c);
  and and_1 (and_1_out, not_1_out, not_2_out, not_3_out);
  and and_2 (and_2_out, not_4_out, b, not_5_out);
  and and_3 (and_3_out, a, not_6_out, not_7_out);
  and and_4 (and_4_out, a, c, not_8_out);
  and and_5 (and_5_out, a, b, not_9_out, d);
  or or_1 (S4, and_1_out, and_2_out, and_3_out, and_4_out, and_5_out);
endmodule
